// Logisim project Goncalves_Lucas_ULA.circ as structural Verilog: 3 circuits, main circuit main
module main (
  input  R_1_W_0,
  input  in_2,
  input  [3:0] in_3,
  output [7:0] out_4,
  output Overflow,
  output Zero
);

  wire clock_1_out, clock_2_out, clock_3_out, not_1_out, not_2_out, uc_1_mod_end, ula_1_overflow, ula_1_zero;
  wire [2:0] uc_1_opcode;
  wire [3:0] AC_q, counter_1_q, multiplexer_1_out, ram_1_data, uc_1_operando, ula_1_out_5;
  wire [7:0] rom_1_data;

  not not_1 (not_1_out, in_2);
  Clock clock_1 (.out(clock_1_out));
  Counter #(.width(4), .max('hf)) counter_1 (
    .load(in_2), .D(in_3), .count(not_1_out), .Q(counter_1_q), .clk(clock_1_out));  // open: carry, clr
  UC uc_1 (.Operando(uc_1_operando), .Mod_End(uc_1_mod_end), .OpCode(uc_1_opcode), .in_1(out_4));
  Register register_1 (.D(rom_1_data), .Q(out_4), .clk(clock_1_out));  // open: en, clr
  ROM #(.addrWidth(4)) rom_1 (.addr(counter_1_q), .data(rom_1_data));  // open: sel
  Clock clock_2 (.out(clock_2_out));
  Multiplexer #(.width(4)) multiplexer_1 (
    .in0(uc_1_operando), .in1(ram_1_data), .out(multiplexer_1_out), .sel(uc_1_mod_end));  // open: en
  ULA ula_1 (
    .A(AC_q), .B(multiplexer_1_out), .in_4(uc_1_opcode), .out_5(ula_1_out_5), .Overflow(ula_1_overflow),
    .Zero(ula_1_zero), .D(uc_1_mod_end));
  Register #(.width(4)) AC (.D(ula_1_out_5), .Q(AC_q));  // open: en, clk, clr
  Clock clock_3 (.out(clock_3_out));
  D_Flip_Flop Ov (.clk(clock_2_out), .D(ula_1_overflow), .Q(Overflow));  // open: Qn, preset, en, reset
  D_Flip_Flop u_Zero (.clk(clock_2_out), .D(ula_1_zero), .Q(Zero));  // open: Qn, preset, en, reset
  RAM #(.addrWidth(4), .dataWidth(4)) ram_1 (
    .addr(uc_1_operando), .data(ram_1_data), .clk(clock_3_out), .ld(R_1_W_0));  // open: sel, clr
  assign ram_1_data = not_2_out ? AC_q : 4'bz;  // Controlled_Buffer controlled_buffer_1
  not not_2 (not_2_out, R_1_W_0);
endmodule

module ULA (
  input  D,
  input  [3:0] A,
  input  [3:0] B,
  input  [2:0] in_4,
  output [3:0] out_5,
  output Overflow,
  output Zero
);

  wire and_1_out, and_2_out, decoder_1_out0, decoder_1_out1, decoder_1_out2, decoder_1_out3, decoder_1_out4,
       decoder_1_out5, decoder_1_out6, decoder_1_out7, not_1_out, subtractor_1_bout;
  wire [3:0] adder_1_out, controlled_buffer_6_out, or_2_out, shifter_1_out, shifter_2_out, subtractor_1_out;

  Decoder #(.select(3)) decoder_1 (
    .out0(decoder_1_out0), .out1(decoder_1_out1), .out2(decoder_1_out2), .out3(decoder_1_out3),
    .out4(decoder_1_out4), .out5(decoder_1_out5), .out6(decoder_1_out6), .out7(decoder_1_out7), .sel(in_4));  // open: en
  assign out_5 = decoder_1_out0 ? B : 4'bz;  // Controlled_Buffer controlled_buffer_1
  and and_1 (and_1_out, decoder_1_out7, decoder_1_out1);
  Adder #(.width(4)) adder_1 (.a(A), .b(B), .out(adder_1_out), .cout(decoder_1_out7));  // open: cin
  assign out_5 = decoder_1_out1 ? adder_1_out : 4'bz;  // Controlled_Buffer controlled_buffer_2
  and and_2 (and_2_out, subtractor_1_bout, decoder_1_out2);
  or or_1 (Overflow, and_1_out, and_2_out);
  Subtractor #(.width(4)) subtractor_1 (.a(A), .b(B), .out(subtractor_1_out), .bout(subtractor_1_bout));  // open: bin
  assign out_5 = decoder_1_out2 ? subtractor_1_out : 4'bz;  // Controlled_Buffer controlled_buffer_3
  assign or_2_out = B | A;  // OR_Gate or_2, 4 bits wide
  assign out_5 = decoder_1_out3 ? or_2_out : 4'bz;  // Controlled_Buffer controlled_buffer_4
  assign out_5 = decoder_1_out4 ? ~B : 4'bz;  // Controlled_Inverter controlled_inverter_1
  assign out_5 = decoder_1_out5 ? controlled_buffer_6_out : 4'bz;  // Controlled_Buffer controlled_buffer_5
  nor nor_1 (Zero, decoder_1_out7, decoder_1_out6, out_5[3], out_5[2], out_5[1], out_5[0]);
  Shifter #(.width(4)) shifter_1 (.in(A), .\dist (B[1:0]), .out(shifter_1_out));
  Shifter #(.width(4), .shift("lr")) shifter_2 (.in(A), .\dist (B[1:0]), .out(shifter_2_out));
  assign controlled_buffer_6_out = D ? shifter_2_out : 4'bz;  // Controlled_Buffer controlled_buffer_6
  not not_1 (not_1_out, D);
  assign controlled_buffer_6_out = not_1_out ? shifter_1_out : 4'bz;  // Controlled_Buffer controlled_buffer_7
endmodule

module UC (
  input  [7:0] in_1,
  output [3:0] Operando,
  output Mod_End,
  output [2:0] OpCode
);


  assign Mod_End = in_1[4];
  assign OpCode = in_1[7:5];
  assign Operando = in_1[3:0];
endmodule
